// Logisim project trabalho1.circ as structural Verilog: 2 circuits, main circuit main
module main (
  output [31:0] out_1
);

  wire button_1_out;
  wire [23:0] parser_1_out_24;
  wire [31:0] adder_1_out, register_1_q;

  Register #(.width(32)) register_1 (.D(adder_1_out), .en(1'b1), .clk(button_1_out), .Q(register_1_q), .clr(1'b0));
  Button button_1 (.out(button_1_out));
  Adder #(.width(32)) adder_1 (.a(32'h4), .b(register_1_q), .out(adder_1_out), .cin(1'b0));  // open: cout
  ROM #(.addrWidth(24), .dataWidth(32)) rom_1 (.addr(parser_1_out_24), .data(out_1));
  Parser parser_1 (.in_32(register_1_q), .out_24(parser_1_out_24));

  // Notes on the sheet:
  //   contents of rom_1 (hex, n*v repeats v):
  //   4f207261 746f2072 6f657520 6120726f 75706120 646f2072 65692064 6520526f 6d610000
endmodule

module Parser (
  input  [31:0] in_32,
  output [23:0] out_24
);


  assign out_24 = in_32[25:2];
endmodule
