// Logisim project trabalho4.circ as structural Verilog: 12 circuits, main circuit main
module main (
  input  pcsrc,
  input  memtoReg,
  input  in_3,
  input  [2:0] alu_op,
  input  in_5,
  input  clear,
  input  in_7,
  input  clock,
  input  regdst,
  input  [1:0] in_10,
  input  in_11,
  input  ALUSrc,
  output alu_zero,
  output out_14
);

  wire [4:0] instruction_memory_1_rd, instruction_memory_1_rs, instruction_memory_1_rt, multiplexer_1_out;
  wire [15:0] instruction_memory_1_immediate;
  wire [31:0] adder_1_out, adder_2_out, alu_1_result, ext_16_32_1_out_32, multiplexer_2_out,
       multiplexer_3_out, multiplexer_4_out, PC_q, ram_memory_1_data_out, registers_1_data_out_1,
       registers_1_data_out_2, sll_2bit_1_out_32;

  Register #(.width(32)) PC (.D(multiplexer_3_out), .en(1'b1), .clk(in_3), .Q(PC_q), .clr(1'b0));
  Adder #(.width(32)) adder_1 (.a(32'h4), .b(PC_q), .out(adder_1_out), .cin(1'b0));  // open: cout
  instruction_memory instruction_memory_1 (
    .rs(instruction_memory_1_rs), .rd(instruction_memory_1_rd), .address_32(PC_q),
    .immediate(instruction_memory_1_immediate), .rt(instruction_memory_1_rt));
  Multiplexer #(.width(5), .enable("false")) multiplexer_1 (
    .in0(instruction_memory_1_rt), .in1(instruction_memory_1_rd), .out(multiplexer_1_out), .sel(regdst));
  ext_16_32 ext_16_32_1 (.out_32(ext_16_32_1_out_32), .in_16(instruction_memory_1_immediate));
  registers registers_1 (
    .data_out_1(registers_1_data_out_1), .write_reg(multiplexer_1_out), .clock(clock),
    .read_reg_1(instruction_memory_1_rs), .clear(clear), .read_reg_2(instruction_memory_1_rt),
    .data_in(multiplexer_4_out), .data_out_2(registers_1_data_out_2));
  sll_2bit sll_2bit_1 (.out_32(sll_2bit_1_out_32), .in_32(ext_16_32_1_out_32));
  Multiplexer #(.width(32), .enable("false")) multiplexer_2 (
    .in0(registers_1_data_out_2), .in1(ext_16_32_1_out_32), .out(multiplexer_2_out), .sel(ALUSrc));
  Adder #(.width(32)) adder_2 (.a(adder_1_out), .b(sll_2bit_1_out_32), .out(adder_2_out), .cin(1'b0));  // open: cout
  Multiplexer #(.width(32), .enable("false")) multiplexer_3 (
    .in0(adder_1_out), .in1(adder_2_out), .out(multiplexer_3_out), .sel(pcsrc));
  alu alu_1 (
    .zero(alu_zero), .value_1(registers_1_data_out_1), .result(alu_1_result), .value_2(multiplexer_2_out),
    .op(alu_op));
  ram_memory ram_memory_1 (
    .address(alu_1_result), .data_in(registers_1_data_out_2), .write_enble(in_5), .output_enable(in_7),
    .whb(in_10), .mem_clock(in_11), .data_out(ram_memory_1_data_out));
  Multiplexer #(.width(32), .enable("false")) multiplexer_4 (
    .in0(alu_1_result), .in1(ram_memory_1_data_out), .out(multiplexer_4_out), .sel(memtoReg));
endmodule

module registers (
  input  [4:0] write_reg,
  input  [4:0] read_reg_1,
  input  [4:0] read_reg_2,
  input  [31:0] data_in,
  input  clear,
  input  clock,
  output [31:0] data_out_1,
  output [31:0] data_out_2
);

  wire we_00, we_01, we_02, we_03, we_04, we_05, we_06, we_07, we_08, we_09, we_10, we_11, we_12, we_13,
       we_14, we_15, we_16, we_17, we_18, we_19, we_20, we_21, we_22, we_23, we_24, we_25, we_26, we_27,
       we_28, we_29, we_30, we_31;
  wire [31:0] register_1_q, register_2_q, register_3_q, register_4_q, register_5_q, register_6_q,
       register_7_q, register_8_q, register_9_q, register_10_q, register_11_q, register_12_q, register_13_q,
       register_14_q, register_15_q, register_16_q, register_17_q, register_18_q, register_19_q,
       register_20_q, register_21_q, register_22_q, register_23_q, register_24_q, register_25_q,
       register_26_q, register_27_q, register_28_q, register_29_q, register_30_q, register_31_q,
       register_32_q;

  Demultiplexer #(.select(5), .enable("false")) demultiplexer_1 (
    .out0(we_00), .out1(we_01), .out2(we_02), .out3(we_03), .out4(we_04), .out5(we_05), .out6(we_06),
    .out7(we_07), .out8(we_08), .out9(we_09), .out10(we_10), .out11(we_11), .out12(we_12), .out13(we_13),
    .out14(we_14), .out15(we_15), .out16(we_16), .out17(we_17), .out18(we_18), .out19(we_19), .out20(we_20),
    .out21(we_21), .out22(we_22), .out23(we_23), .out24(we_24), .out25(we_25), .out26(we_26), .out27(we_27),
    .out28(we_28), .out29(we_29), .out30(we_30), .out31(we_31), .in(1'b1), .sel(write_reg));
  Register #(.width(32)) register_1 (.D(data_in), .en(we_00), .clk(clock), .Q(register_1_q), .clr(1'b1));
  Register #(.width(32)) register_2 (.D(data_in), .en(we_01), .clk(clock), .Q(register_2_q), .clr(clear));
  Register #(.width(32)) register_3 (.D(data_in), .en(we_02), .clk(clock), .Q(register_3_q), .clr(clear));
  Register #(.width(32)) register_4 (.D(data_in), .en(we_03), .clk(clock), .Q(register_4_q), .clr(clear));
  Register #(.width(32)) register_5 (.D(data_in), .en(we_04), .clk(clock), .Q(register_5_q), .clr(clear));
  Register #(.width(32)) register_6 (.D(data_in), .en(we_05), .clk(clock), .Q(register_6_q), .clr(clear));
  Register #(.width(32)) register_7 (.D(data_in), .en(we_06), .clk(clock), .Q(register_7_q), .clr(clear));
  Register #(.width(32)) register_8 (.D(data_in), .en(we_07), .clk(clock), .Q(register_8_q), .clr(clear));
  Register #(.width(32)) register_9 (.D(data_in), .en(we_08), .clk(clock), .Q(register_9_q), .clr(clear));
  Register #(.width(32)) register_10 (.D(data_in), .en(we_09), .clk(clock), .Q(register_10_q), .clr(clear));
  Register #(.width(32)) register_11 (.D(data_in), .en(we_10), .clk(clock), .Q(register_11_q), .clr(clear));
  Register #(.width(32)) register_12 (.D(data_in), .en(we_11), .clk(clock), .Q(register_12_q), .clr(clear));
  Register #(.width(32)) register_13 (.D(data_in), .en(we_12), .clk(clock), .Q(register_13_q), .clr(clear));
  Register #(.width(32)) register_14 (.D(data_in), .en(we_13), .clk(clock), .Q(register_14_q), .clr(clear));
  Register #(.width(32)) register_15 (.D(data_in), .en(we_14), .clk(clock), .Q(register_15_q), .clr(clear));
  Register #(.width(32)) register_16 (.D(data_in), .en(we_15), .clk(clock), .Q(register_16_q), .clr(clear));
  Register #(.width(32)) register_17 (.D(data_in), .en(we_16), .clk(clock), .Q(register_17_q), .clr(clear));
  Register #(.width(32)) register_18 (.D(data_in), .en(we_17), .clk(clock), .Q(register_18_q), .clr(clear));
  Register #(.width(32)) register_19 (.D(data_in), .en(we_18), .clk(clock), .Q(register_19_q), .clr(clear));
  Register #(.width(32)) register_20 (.D(data_in), .en(we_19), .clk(clock), .Q(register_20_q), .clr(clear));
  Register #(.width(32)) register_21 (.D(data_in), .en(we_20), .clk(clock), .Q(register_21_q), .clr(clear));
  Register #(.width(32)) register_22 (.D(data_in), .en(we_21), .clk(clock), .Q(register_22_q), .clr(clear));
  Register #(.width(32)) register_23 (.D(data_in), .en(we_22), .clk(clock), .Q(register_23_q), .clr(clear));
  Register #(.width(32)) register_24 (.D(data_in), .en(we_23), .clk(clock), .Q(register_24_q), .clr(clear));
  Register #(.width(32)) register_25 (.D(data_in), .en(we_24), .clk(clock), .Q(register_25_q), .clr(clear));
  Register #(.width(32)) register_26 (.D(data_in), .en(we_25), .clk(clock), .Q(register_26_q), .clr(clear));
  Register #(.width(32)) register_27 (.D(data_in), .en(we_26), .clk(clock), .Q(register_27_q), .clr(clear));
  Register #(.width(32)) register_28 (.D(data_in), .en(we_27), .clk(clock), .Q(register_28_q), .clr(clear));
  Register #(.width(32)) register_29 (.D(data_in), .en(we_28), .clk(clock), .Q(register_29_q), .clr(clear));
  Register #(.width(32)) register_30 (.D(data_in), .en(we_29), .clk(clock), .Q(register_30_q), .clr(clear));
  Register #(.width(32)) register_31 (.D(data_in), .en(we_30), .clk(clock), .Q(register_31_q), .clr(clear));
  Register #(.width(32)) register_32 (.D(data_in), .en(we_31), .clk(clock), .Q(register_32_q), .clr(clear));
  Multiplexer #(.select(5), .width(32), .enable("false")) multiplexer_1 (
    .in0(register_1_q), .in1(register_2_q), .in2(register_3_q), .in3(register_4_q), .in4(register_5_q),
    .in5(register_6_q), .in6(register_7_q), .in7(register_8_q), .in8(register_9_q), .in9(register_10_q),
    .in10(register_11_q), .in11(register_12_q), .in12(register_13_q), .in13(register_14_q),
    .in14(register_15_q), .in15(register_16_q), .in16(register_17_q), .in17(register_18_q),
    .in18(register_19_q), .in19(register_20_q), .in20(register_21_q), .in21(register_22_q),
    .in22(register_23_q), .in23(register_24_q), .in24(register_25_q), .in25(register_26_q),
    .in26(register_27_q), .in27(register_28_q), .in28(register_29_q), .in29(register_30_q),
    .in30(register_31_q), .in31(register_32_q), .out(data_out_1), .sel(read_reg_1));
  Multiplexer #(.select(5), .width(32), .enable("false")) multiplexer_2 (
    .in0(register_1_q), .in1(register_2_q), .in2(register_3_q), .in3(register_4_q), .in4(register_5_q),
    .in5(register_6_q), .in6(register_7_q), .in7(register_8_q), .in8(register_9_q), .in9(register_10_q),
    .in10(register_11_q), .in11(register_12_q), .in12(register_13_q), .in13(register_14_q),
    .in14(register_15_q), .in15(register_16_q), .in16(register_17_q), .in17(register_18_q),
    .in18(register_19_q), .in19(register_20_q), .in20(register_21_q), .in21(register_22_q),
    .in22(register_23_q), .in23(register_24_q), .in24(register_25_q), .in25(register_26_q),
    .in26(register_27_q), .in27(register_28_q), .in28(register_29_q), .in29(register_30_q),
    .in30(register_31_q), .in31(register_32_q), .out(data_out_2), .sel(read_reg_2));

  // Other names for the same wires on the sheet: value[31:0] = data_in
endmodule

module alu (
  input  [31:0] value_1,
  input  [31:0] value_2,
  input  [2:0] op,
  output [31:0] result,
  output zero
);

  wire [31:0] adder_1_out, and_1_out, nor_1_out, or_1_out, subtractor_1_out;

  Adder #(.width(32)) adder_1 (.a(value_1), .b(value_2), .out(adder_1_out), .cin(1'b0));  // open: cout
  Subtractor #(.width(32)) subtractor_1 (.a(value_1), .b(value_2), .out(subtractor_1_out), .bin(1'b0));  // open: bout
  assign and_1_out = value_1 & value_2;  // AND_Gate and_1, 32 bits wide
  assign or_1_out = value_1 | value_2;  // OR_Gate or_1, 32 bits wide
  assign nor_1_out = ~(value_1 | value_2);  // NOR_Gate nor_1, 32 bits wide
  Multiplexer #(.select(3), .width(32), .enable("false")) multiplexer_1 (
    .in0(adder_1_out), .in1(subtractor_1_out), .in2(and_1_out), .in3(or_1_out), .in4(nor_1_out),
    .out(result), .sel(op));  // open: in5, in6, in7
  or32x1 or32x1_1 (.in_32(result), .zero(zero));
endmodule

module ram_memory (
  input  [31:0] address,
  input  [31:0] data_in,
  input  write_enble,
  input  output_enable,
  input  [1:0] whb,
  input  mem_clock,
  output [31:0] data_out
);

  wire a1;
  wire [1:0] a1a0;
  wire [7:0] byte_in_00, byte_in_01, byte_in_10, byte_in_11, byte_out_00, byte_out_01, byte_out_10,
       byte_out_11, demultiplexer_2_out0, demultiplexer_2_out1, demultiplexer_2_out2, demultiplexer_2_out3,
       multiplexer_3_out;
  wire [15:0] demultiplexer_1_out0, demultiplexer_1_out1, multiplexer_2_out;
  wire [23:0] address_t;
  wire [31:0] ext_8_32_1_out_32, ext_16_32_1_out_32;

  address_spliter address_spliter_1 (.full_address(address), .a1(a1), .a1a0(a1a0), .address(address_t));
  Demultiplexer #(.width(16), .enable("false")) demultiplexer_1 (
    .out0(demultiplexer_1_out0), .out1(demultiplexer_1_out1), .in(data_in[15:0]), .sel(a1));
  Demultiplexer #(.select(2), .width(8), .enable("false")) demultiplexer_2 (
    .out0(demultiplexer_2_out0), .out1(demultiplexer_2_out1), .out2(demultiplexer_2_out2),
    .out3(demultiplexer_2_out3), .in(data_in[7:0]), .sel(a1a0));
  Multiplexer #(.select(2), .width(32), .enable("false")) multiplexer_1 (
    .in0(data_in), .in1({demultiplexer_1_out1, demultiplexer_1_out0}),
    .in2({demultiplexer_2_out3, demultiplexer_2_out2, demultiplexer_2_out1, demultiplexer_2_out0}),
    .out({byte_in_11, byte_in_10, byte_in_01, byte_in_00}), .sel(whb));  // open: in3
  RAM #(.addrWidth(24), .databus("bibus")) ram_1 (
    .addr(address_t), .we(write_enble), .oe(output_enable), .clk(mem_clock), .din(byte_in_00),
    .dout(byte_out_00));
  RAM #(.addrWidth(24), .databus("bibus")) ram_2 (
    .addr(address_t), .we(write_enble), .oe(output_enable), .clk(mem_clock), .din(byte_in_10),
    .dout(byte_out_10));
  RAM #(.addrWidth(24), .databus("bibus")) ram_3 (
    .addr(address_t), .we(write_enble), .oe(output_enable), .clk(mem_clock), .din(byte_in_01),
    .dout(byte_out_01));
  RAM #(.addrWidth(24), .databus("bibus")) ram_4 (
    .addr(address_t), .we(write_enble), .oe(output_enable), .clk(mem_clock), .din(byte_in_11),
    .dout(byte_out_11));
  Multiplexer #(.width(16), .enable("false")) multiplexer_2 (
    .in0({byte_out_01, byte_out_00}), .in1({byte_out_11, byte_out_10}), .out(multiplexer_2_out), .sel(a1));
  Multiplexer #(.select(2), .width(8), .enable("false")) multiplexer_3 (
    .in0(byte_out_00), .in1(byte_out_01), .in2(byte_out_10), .in3(byte_out_11), .out(multiplexer_3_out),
    .sel(a1a0));
  ext_16_32 ext_16_32_1 (.out_32(ext_16_32_1_out_32), .in_16(multiplexer_2_out));
  ext_8_32 ext_8_32_1 (.out_32(ext_8_32_1_out_32), .in_8(multiplexer_3_out));
  Multiplexer #(.select(2), .width(32), .enable("false")) multiplexer_4 (
    .in0({byte_out_11, byte_out_10, byte_out_01, byte_out_00}), .in1(ext_16_32_1_out_32),
    .in2(ext_8_32_1_out_32), .out(data_out), .sel(whb));  // open: in3

  // Other names for the same wires on the sheet: clock = mem_clock; byte_in[7:0] = data_in[7:0];
  //   half_in[15:0] = data_in[15:0]; word_in[31:0] = data_in; half_out_0[15:0] = {byte_out_01, byte_out_00};
  //   word_out[31:0] = {byte_out_11, byte_out_10, byte_out_01, byte_out_00};
  //   half_out_1[15:0] = {byte_out_11, byte_out_10}; write_enable = write_enble
endmodule

module instruction_memory (
  input  [31:0] address_32,
  output [15:0] immediate,
  output [4:0] rd,
  output [4:0] rt,
  output [4:0] rs
);

  wire [31:26] rom_1_data;

  ROM #(.addrWidth(24), .dataWidth(32)) rom_1 (.addr(address_32[25:2]), .data({rom_1_data, rs, rt, immediate}));

  assign rd = immediate[15:11];
endmodule

module or32x1 (
  input  [31:0] in_32,
  output zero
);

  nor nor_1 (zero, in_32[0], in_32[1], in_32[2], in_32[3], in_32[4], in_32[5], in_32[6], in_32[7], in_32[8], in_32[9], in_32[10], in_32[11], in_32[12], in_32[13], in_32[14], in_32[15], in_32[17], in_32[18], in_32[19], in_32[20], in_32[21], in_32[22], in_32[23], in_32[24], in_32[25], in_32[26], in_32[27], in_32[28], in_32[29], in_32[30], in_32[31], in_32[16]);
endmodule

module address_spliter (
  input  [31:0] full_address,
  output a1,
  output [1:0] a1a0,
  output [23:0] address
);


  assign a1 = full_address[1];
  assign a1a0 = full_address[1:0];
  assign address = full_address[25:2];
endmodule

module sll_2bit (
  input  [31:0] in_32,
  output [31:0] out_32
);


  assign out_32 = {in_32[29:0], 2'b00};
endmodule

module ext_16_32 (
  input  [15:0] in_16,
  output [31:0] out_32
);


  assign out_32 = {{16{1'b0}}, in_16};
endmodule

module ext_8_32 (
  input  [7:0] in_8,
  output [31:0] out_32
);


  assign out_32 = {{24{1'b0}}, in_8};
endmodule

module control_unit (
  input  [5:0] in_1
);

  ROM #(.addrWidth(6)) rom_1 (.addr(in_1));  // open: data
endmodule

module alu_control (
  input  [5:0] in_1,
  input  [2:0] aluOP
);

  Demultiplexer #(.select(3), .enable("false")) demultiplexer_1 (.sel(aluOP));  // open: out0, out1, out2, out3, out4, out5, out6, out7, in
endmodule
