// Logisim project trabalho5.circ as structural Verilog: 15 circuits, main circuit main
module main (
  input  in_1
);

  wire alu_1_zero, alu_control_1_jumpregister, and_1_out, clear_out, clock_out, control_unit_1_alusrc,
       control_unit_1_branch, control_unit_1_jump, control_unit_1_memread, control_unit_1_memtoreg,
       control_unit_1_memwrite, control_unit_1_regdst, control_unit_1_regwrite;
  wire [1:0] control_unit_1_whb;
  wire [3:0] control_unit_1_aluop;
  wire [4:0] instruction_memory_1_rd, instruction_memory_1_rs, instruction_memory_1_rt, multiplexer_1_out,
       multiplexer_2_out;
  wire [5:0] alu_control_1_aluctrlout, instruction_memory_1_func, instruction_memory_1_op_code;
  wire [15:0] instruction_memory_1_immediate;
  wire [25:0] instruction_memory_1_jump_target;
  wire [31:0] adder_1_out, adder_2_out, alu_1_result, ext_16_32_1_out_32, multiplexer_3_out,
       multiplexer_4_out, multiplexer_5_out, multiplexer_6_out, multiplexer_7_out, multiplexer_8_out, PC_q,
       ram_memory_1_data_out, registers_1_data_out_1, registers_1_data_out_2, sll_2_1_out_32,
       target_calc_1_target_out;

  Register #(.width(32)) PC (.D(multiplexer_3_out), .en(1'b1), .clk(clock_out), .Q(PC_q), .clr(in_1));
  Button clock (.out(clock_out));
  Adder #(.width(32)) adder_1 (.a(32'h4), .b(PC_q), .out(adder_1_out), .cin(1'b0));  // open: cout
  instruction_memory instruction_memory_1 (
    .rs(instruction_memory_1_rs), .rt(instruction_memory_1_rt), .immediate(instruction_memory_1_immediate),
    .rd(instruction_memory_1_rd), .address_32(PC_q), .op_code(instruction_memory_1_op_code),
    .func(instruction_memory_1_func), .Jump_Target(instruction_memory_1_jump_target));  // open: shamt
  control_unit control_unit_1 (
    .op_code(instruction_memory_1_op_code), .jump(control_unit_1_jump), .RegDst(control_unit_1_regdst),
    .Branch(control_unit_1_branch), .MemRead(control_unit_1_memread), .MemToReg(control_unit_1_memtoreg),
    .ALUOp(control_unit_1_aluop), .MemWrite(control_unit_1_memwrite), .ALUSrc(control_unit_1_alusrc),
    .RegWrite(control_unit_1_regwrite), .whb(control_unit_1_whb));
  Multiplexer #(.width(5), .enable("false")) multiplexer_1 (
    .in0(instruction_memory_1_rt), .in1(instruction_memory_1_rd), .out(multiplexer_1_out),
    .sel(control_unit_1_regdst));
  target_calc target_calc_1 (
    .jmp_target(instruction_memory_1_jump_target), .pc_plus_4(adder_1_out),
    .target_out(target_calc_1_target_out));
  Multiplexer #(.width(5), .enable("false")) multiplexer_2 (
    .in0(multiplexer_1_out), .in1({5{1'b1}}), .out(multiplexer_2_out), .sel(control_unit_1_jump));
  Button clear (.out(clear_out));
  ext_16_32 ext_16_32_1 (.out_32(ext_16_32_1_out_32), .in_16(instruction_memory_1_immediate));
  Multiplexer #(.width(32), .enable("false")) multiplexer_3 (
    .in0(multiplexer_6_out), .in1(registers_1_data_out_1), .out(multiplexer_3_out),
    .sel(alu_control_1_jumpregister));
  registers registers_1 (
    .data_out_1(registers_1_data_out_1), .clear(clear_out), .read_reg_2(instruction_memory_1_rt),
    .write_reg(multiplexer_2_out), .read_reg_1(instruction_memory_1_rs), .data_in(multiplexer_8_out),
    .clock(clock_out), .data_out_2(registers_1_data_out_2), .write_enable(control_unit_1_regwrite));
  alu_control alu_control_1 (
    .ALUOp(control_unit_1_aluop), .func(instruction_memory_1_func),
    .JumpRegister(alu_control_1_jumpregister), .ALUCtrlOut(alu_control_1_aluctrlout));
  sll_2 sll_2_1 (.out_32(sll_2_1_out_32), .in_32(ext_16_32_1_out_32));
  Multiplexer #(.width(32), .enable("false")) multiplexer_4 (
    .in0(registers_1_data_out_2), .in1(ext_16_32_1_out_32), .out(multiplexer_4_out),
    .sel(control_unit_1_alusrc));
  Adder #(.width(32)) adder_2 (.a(adder_1_out), .b(sll_2_1_out_32), .out(adder_2_out), .cin(1'b0));  // open: cout
  alu alu_1 (
    .zero(alu_1_zero), .value_2(multiplexer_4_out), .result(alu_1_result), .op(alu_control_1_aluctrlout),
    .value_1(registers_1_data_out_1));
  and and_1 (and_1_out, alu_1_zero, control_unit_1_branch);
  Multiplexer #(.width(32), .enable("false")) multiplexer_5 (
    .in0(adder_1_out), .in1(adder_2_out), .out(multiplexer_5_out), .sel(and_1_out));
  Multiplexer #(.width(32), .enable("false")) multiplexer_6 (
    .in0(multiplexer_5_out), .in1(target_calc_1_target_out), .out(multiplexer_6_out),
    .sel(control_unit_1_jump));
  Multiplexer #(.width(32), .enable("false")) multiplexer_7 (
    .in0(alu_1_result), .in1(ram_memory_1_data_out), .out(multiplexer_7_out), .sel(control_unit_1_memtoreg));
  ram_memory ram_memory_1 (
    .address(alu_1_result), .data_in(registers_1_data_out_2), .write_enble(control_unit_1_memwrite),
    .output_enable(control_unit_1_memread), .whb(control_unit_1_whb), .mem_clock(clock_out),
    .data_out(ram_memory_1_data_out));
  Multiplexer #(.width(32), .enable("false")) multiplexer_8 (
    .in0(multiplexer_7_out), .in1(adder_1_out), .out(multiplexer_8_out), .sel(control_unit_1_jump));
endmodule

module registers (
  input  [4:0] write_reg,
  input  [4:0] read_reg_1,
  input  [4:0] read_reg_2,
  input  [31:0] data_in,
  input  clear,
  input  clock,
  input  write_enable,
  output [31:0] data_out_1,
  output [31:0] data_out_2
);

  wire we_00, we_01, we_02, we_03, we_04, we_05, we_06, we_07, we_08, we_09, we_10, we_11, we_12, we_13,
       we_14, we_15, we_16, we_17, we_18, we_19, we_20, we_21, we_22, we_23, we_24, we_25, we_26, we_27,
       we_28, we_29, we_30, we_31;
  wire [31:0] register_1_q, register_2_q, register_3_q, register_4_q, register_5_q, register_6_q,
       register_7_q, register_8_q, register_9_q, register_10_q, register_11_q, register_12_q, register_13_q,
       register_14_q, register_15_q, register_16_q, register_17_q, register_18_q, register_19_q,
       register_20_q, register_21_q, register_22_q, register_23_q, register_24_q, register_25_q,
       register_26_q, register_27_q, register_28_q, register_29_q, register_30_q, register_31_q,
       register_32_q;

  Demultiplexer #(.select(5), .enable("false")) demultiplexer_1 (
    .out0(we_00), .out1(we_01), .out2(we_02), .out3(we_03), .out4(we_04), .out5(we_05), .out6(we_06),
    .out7(we_07), .out8(we_08), .out9(we_09), .out10(we_10), .out11(we_11), .out12(we_12), .out13(we_13),
    .out14(we_14), .out15(we_15), .out16(we_16), .out17(we_17), .out18(we_18), .out19(we_19), .out20(we_20),
    .out21(we_21), .out22(we_22), .out23(we_23), .out24(we_24), .out25(we_25), .out26(we_26), .out27(we_27),
    .out28(we_28), .out29(we_29), .out30(we_30), .out31(we_31), .in(write_enable), .sel(write_reg));
  Register #(.width(32)) register_1 (.D(data_in), .en(we_00), .clk(clock), .Q(register_1_q), .clr(1'b1));
  Register #(.width(32)) register_2 (.D(data_in), .en(we_01), .clk(clock), .Q(register_2_q), .clr(clear));
  Register #(.width(32)) register_3 (.D(data_in), .en(we_02), .clk(clock), .Q(register_3_q), .clr(clear));
  Register #(.width(32)) register_4 (.D(data_in), .en(we_03), .clk(clock), .Q(register_4_q), .clr(clear));
  Register #(.width(32)) register_5 (.D(data_in), .en(we_04), .clk(clock), .Q(register_5_q), .clr(clear));
  Register #(.width(32)) register_6 (.D(data_in), .en(we_05), .clk(clock), .Q(register_6_q), .clr(clear));
  Register #(.width(32)) register_7 (.D(data_in), .en(we_06), .clk(clock), .Q(register_7_q), .clr(clear));
  Register #(.width(32)) register_8 (.D(data_in), .en(we_07), .clk(clock), .Q(register_8_q), .clr(clear));
  Register #(.width(32)) register_9 (.D(data_in), .en(we_08), .clk(clock), .Q(register_9_q), .clr(clear));
  Register #(.width(32)) register_10 (.D(data_in), .en(we_09), .clk(clock), .Q(register_10_q), .clr(clear));
  Register #(.width(32)) register_11 (.D(data_in), .en(we_10), .clk(clock), .Q(register_11_q), .clr(clear));
  Register #(.width(32)) register_12 (.D(data_in), .en(we_11), .clk(clock), .Q(register_12_q), .clr(clear));
  Register #(.width(32)) register_13 (.D(data_in), .en(we_12), .clk(clock), .Q(register_13_q), .clr(clear));
  Register #(.width(32)) register_14 (.D(data_in), .en(we_13), .clk(clock), .Q(register_14_q), .clr(clear));
  Register #(.width(32)) register_15 (.D(data_in), .en(we_14), .clk(clock), .Q(register_15_q), .clr(clear));
  Register #(.width(32)) register_16 (.D(data_in), .en(we_15), .clk(clock), .Q(register_16_q), .clr(clear));
  Register #(.width(32)) register_17 (.D(data_in), .en(we_16), .clk(clock), .Q(register_17_q), .clr(clear));
  Register #(.width(32)) register_18 (.D(data_in), .en(we_17), .clk(clock), .Q(register_18_q), .clr(clear));
  Register #(.width(32)) register_19 (.D(data_in), .en(we_18), .clk(clock), .Q(register_19_q), .clr(clear));
  Register #(.width(32)) register_20 (.D(data_in), .en(we_19), .clk(clock), .Q(register_20_q), .clr(clear));
  Register #(.width(32)) register_21 (.D(data_in), .en(we_20), .clk(clock), .Q(register_21_q), .clr(clear));
  Register #(.width(32)) register_22 (.D(data_in), .en(we_21), .clk(clock), .Q(register_22_q), .clr(clear));
  Register #(.width(32)) register_23 (.D(data_in), .en(we_22), .clk(clock), .Q(register_23_q), .clr(clear));
  Register #(.width(32)) register_24 (.D(data_in), .en(we_23), .clk(clock), .Q(register_24_q), .clr(clear));
  Register #(.width(32)) register_25 (.D(data_in), .en(we_24), .clk(clock), .Q(register_25_q), .clr(clear));
  Register #(.width(32)) register_26 (.D(data_in), .en(we_25), .clk(clock), .Q(register_26_q), .clr(clear));
  Register #(.width(32)) register_27 (.D(data_in), .en(we_26), .clk(clock), .Q(register_27_q), .clr(clear));
  Register #(.width(32)) register_28 (.D(data_in), .en(we_27), .clk(clock), .Q(register_28_q), .clr(clear));
  Register #(.width(32)) register_29 (.D(data_in), .en(we_28), .clk(clock), .Q(register_29_q), .clr(clear));
  Register #(.width(32)) register_30 (.D(data_in), .en(we_29), .clk(clock), .Q(register_30_q), .clr(clear));
  Register #(.width(32)) register_31 (.D(data_in), .en(we_30), .clk(clock), .Q(register_31_q), .clr(clear));
  Register #(.width(32)) register_32 (.D(data_in), .en(we_31), .clk(clock), .Q(register_32_q), .clr(clear));
  Multiplexer #(.select(5), .width(32), .enable("false")) multiplexer_1 (
    .in0(register_1_q), .in1(register_2_q), .in2(register_3_q), .in3(register_4_q), .in4(register_5_q),
    .in5(register_6_q), .in6(register_7_q), .in7(register_8_q), .in8(register_9_q), .in9(register_10_q),
    .in10(register_11_q), .in11(register_12_q), .in12(register_13_q), .in13(register_14_q),
    .in14(register_15_q), .in15(register_16_q), .in16(register_17_q), .in17(register_18_q),
    .in18(register_19_q), .in19(register_20_q), .in20(register_21_q), .in21(register_22_q),
    .in22(register_23_q), .in23(register_24_q), .in24(register_25_q), .in25(register_26_q),
    .in26(register_27_q), .in27(register_28_q), .in28(register_29_q), .in29(register_30_q),
    .in30(register_31_q), .in31(register_32_q), .out(data_out_1), .sel(read_reg_1));
  Multiplexer #(.select(5), .width(32), .enable("false")) multiplexer_2 (
    .in0(register_1_q), .in1(register_2_q), .in2(register_3_q), .in3(register_4_q), .in4(register_5_q),
    .in5(register_6_q), .in6(register_7_q), .in7(register_8_q), .in8(register_9_q), .in9(register_10_q),
    .in10(register_11_q), .in11(register_12_q), .in12(register_13_q), .in13(register_14_q),
    .in14(register_15_q), .in15(register_16_q), .in16(register_17_q), .in17(register_18_q),
    .in18(register_19_q), .in19(register_20_q), .in20(register_21_q), .in21(register_22_q),
    .in22(register_23_q), .in23(register_24_q), .in24(register_25_q), .in25(register_26_q),
    .in26(register_27_q), .in27(register_28_q), .in28(register_29_q), .in29(register_30_q),
    .in30(register_31_q), .in31(register_32_q), .out(data_out_2), .sel(read_reg_2));

  // Other names for the same wires on the sheet: value[31:0] = data_in
endmodule

module alu (
  input  [31:0] value_1,
  input  [31:0] value_2,
  input  [5:0] op,
  output [31:0] result,
  output zero
);

  wire or32x1_1_out_32;
  wire [31:0] adder_1_out, and_1_out, bne_comparator_1_out_32, nor_1_out, or_1_out, sll_16_1_out_32,
       subtractor_1_out;

  Adder #(.width(32)) adder_1 (.a(value_1), .b(value_2), .out(adder_1_out), .cin(1'b0));  // open: cout
  Subtractor #(.width(32)) subtractor_1 (.a(value_1), .b(value_2), .out(subtractor_1_out), .bin(1'b0));  // open: bout
  assign and_1_out = value_1 & value_2;  // AND_Gate and_1, 32 bits wide
  assign or_1_out = value_1 | value_2;  // OR_Gate or_1, 32 bits wide
  assign nor_1_out = ~(value_1 | value_2);  // NOR_Gate nor_1, 32 bits wide
  sll_16 sll_16_1 (.in_32(value_2), .out_32(sll_16_1_out_32));
  bne_comparator bne_comparator_1 (.out_32(bne_comparator_1_out_32), .in1_32(value_2), .in0_32(value_1));
  Multiplexer #(.select(4), .width(32), .enable("false")) multiplexer_1 (
    .in0(adder_1_out), .in1(adder_1_out), .in2(subtractor_1_out), .in3(subtractor_1_out), .in4(and_1_out),
    .in5(or_1_out), .in6({32{1'b0}}), .in7(nor_1_out), .in8({32{1'b0}}), .in9(sll_16_1_out_32),
    .in10(bne_comparator_1_out_32), .in11({32{1'b0}}), .in12({32{1'b0}}), .in13({32{1'b0}}),
    .in14({32{1'b0}}), .in15({32{1'b0}}), .out(result), .sel(op[3:0]));
  or32x1 or32x1_1 (.in_32(result), .out_32(or32x1_1_out_32));
  not not_1 (zero, or32x1_1_out_32);

  // Notes on the sheet:
  //   lui
  //   Default
endmodule

module ram_memory (
  input  [31:0] address,
  input  [31:0] data_in,
  input  write_enble,
  input  output_enable,
  input  [1:0] whb,
  input  mem_clock,
  output [31:0] data_out
);

  wire a1;
  wire [1:0] a1a0;
  wire [7:0] byte_in_00, byte_in_01, byte_in_10, byte_in_11, byte_out_00, byte_out_01, byte_out_10,
       byte_out_11, demultiplexer_1_out0, demultiplexer_1_out1, demultiplexer_1_out2, demultiplexer_1_out3,
       multiplexer_2_out;
  wire [15:0] demultiplexer_2_out0, demultiplexer_2_out1, multiplexer_3_out;
  wire [23:0] address_t;
  wire [31:0] ext_8_32_1_out_32, ext_16_32_1_out_32;

  address_spliter address_spliter_1 (.full_address(address), .a1(a1), .a1a0(a1a0), .address(address_t));
  Demultiplexer #(.select(2), .width(8), .enable("false")) demultiplexer_1 (
    .out0(demultiplexer_1_out0), .out1(demultiplexer_1_out1), .out2(demultiplexer_1_out2),
    .out3(demultiplexer_1_out3), .in(data_in[7:0]), .sel(a1a0));
  Demultiplexer #(.width(16), .enable("false")) demultiplexer_2 (
    .out0(demultiplexer_2_out0), .out1(demultiplexer_2_out1), .in(data_in[15:0]), .sel(a1));
  Multiplexer #(.select(2), .width(32), .enable("false")) multiplexer_1 (
    .in0({demultiplexer_1_out3, demultiplexer_1_out2, demultiplexer_1_out1, demultiplexer_1_out0}),
    .in1({demultiplexer_2_out1, demultiplexer_2_out0}), .in3(data_in),
    .out({byte_in_11, byte_in_10, byte_in_01, byte_in_00}), .sel(whb));  // open: in2
  RAM #(.addrWidth(24), .trigger("falling"), .databus("bibus")) ram_1 (
    .addr(address_t), .we(write_enble), .oe(output_enable), .clk(mem_clock), .din(byte_in_00),
    .dout(byte_out_00));
  RAM #(.addrWidth(24), .trigger("falling"), .databus("bibus")) ram_2 (
    .addr(address_t), .we(write_enble), .oe(output_enable), .clk(mem_clock), .din(byte_in_10),
    .dout(byte_out_10));
  RAM #(.addrWidth(24), .trigger("falling"), .databus("bibus")) ram_3 (
    .addr(address_t), .we(write_enble), .oe(output_enable), .clk(mem_clock), .din(byte_in_01),
    .dout(byte_out_01));
  RAM #(.addrWidth(24), .trigger("falling"), .databus("bibus")) ram_4 (
    .addr(address_t), .we(write_enble), .oe(output_enable), .clk(mem_clock), .din(byte_in_11),
    .dout(byte_out_11));
  Multiplexer #(.select(2), .width(8), .enable("false")) multiplexer_2 (
    .in0(byte_out_00), .in1(byte_out_01), .in2(byte_out_10), .in3(byte_out_11), .out(multiplexer_2_out),
    .sel(a1a0));
  Multiplexer #(.width(16), .enable("false")) multiplexer_3 (
    .in0({byte_out_01, byte_out_00}), .in1({byte_out_11, byte_out_10}), .out(multiplexer_3_out), .sel(a1));
  ext_8_32 ext_8_32_1 (.out_32(ext_8_32_1_out_32), .in_8(multiplexer_2_out));
  ext_16_32 ext_16_32_1 (.out_32(ext_16_32_1_out_32), .in_16(multiplexer_3_out));
  Multiplexer #(.select(2), .width(32), .enable("false")) multiplexer_4 (
    .in0(ext_8_32_1_out_32), .in1(ext_16_32_1_out_32),
    .in3({byte_out_11, byte_out_10, byte_out_01, byte_out_00}), .out(data_out), .sel(whb));  // open: in2

  // Other names for the same wires on the sheet: clock = mem_clock; byte_in[7:0] = data_in[7:0];
  //   half_in[15:0] = data_in[15:0]; word_in[31:0] = data_in; half_out_0[15:0] = {byte_out_01, byte_out_00};
  //   word_out[31:0] = {byte_out_11, byte_out_10, byte_out_01, byte_out_00};
  //   half_out_1[15:0] = {byte_out_11, byte_out_10}; write_enable = write_enble
endmodule

module instruction_memory (
  input  [31:0] address_32,
  output [25:0] Jump_Target,
  output [5:0] func,
  output [4:0] shamt,
  output [15:0] immediate,
  output [4:0] rd,
  output [4:0] rt,
  output [4:0] rs,
  output [5:0] op_code
);

  ROM #(.addrWidth(24), .dataWidth(32)) rom_1 (
    .addr(address_32[25:2]), .data({op_code, Jump_Target[25:16], immediate[15:6], func}));

  assign immediate[5:0] = func;
  assign Jump_Target[15:0] = {immediate[15:6], func};
  assign rd = immediate[15:11];
  assign rs = Jump_Target[25:21];
  assign rt = Jump_Target[20:16];
  assign shamt = immediate[10:6];

  // Notes on the sheet:
  //   contents of rom_1 (hex, n*v repeats v):
  //   201d0404 3c0effff 35ceffff 3c0fffff 35effff8 20040005 20050006 c000009 8000008 10a0000a 3afe820
  //   afa50000 afbf0004 ae2820 c000009 8fa50000 8fbf0004 23bd0008 441020 3e00008 20020000 3e00008
  //   Este programa multiplica 2 numeros inteiro sem sinal
  //   Neste caso, muntiplica 5 por 6 e salva em $a0
endmodule

module control_unit (
  input  [5:0] op_code,
  output jump,
  output RegDst,
  output Branch,
  output MemRead,
  output MemToReg,
  output [3:0] ALUOp,
  output MemWrite,
  output ALUSrc,
  output RegWrite,
  output [1:0] whb
);

  ROM #(.addrWidth(6), .dataWidth(12)) rom_1 (
    .addr(op_code), .data({RegWrite, ALUSrc, MemWrite, ALUOp, MemToReg, MemRead, Branch, RegDst, jump}));

  assign whb = op_code[1:0];

  // Notes on the sheet:
  //   contents of rom_1 (hex, n*v repeats v):
  //   802 0 1c1 9e1 24 44 0 0 c60 c80 0 0 ca0 cc0 0 ce0 19*0 d18 d38 d58 0 0 760 780 0 7a0
endmodule

module alu_control (
  input  [3:0] ALUOp,
  input  [5:0] func,
  output JumpRegister,
  output [5:0] ALUCtrlOut
);

  Multiplexer #(.select(4), .width(6), .enable("false")) multiplexer_1 (
    .in0(func), .in1(6'b000010), .in2(6'b001010), .in3({6{1'b0}}), .in4({6{1'b0}}), .in5(6'b000100),
    .in6(6'b000101), .in7(6'b001001), .in8({6{1'b0}}), .in9({6{1'b0}}), .in10({6{1'b0}}), .in11({6{1'b0}}),
    .in12({6{1'b0}}), .in13({6{1'b0}}), .in14({6{1'b0}}), .in15({6{1'b0}}), .out(ALUCtrlOut), .sel(ALUOp));
  Comparator #(.width(6)) comparator_1 (.a(ALUCtrlOut), .b(6'b001000), .eq(JumpRegister));  // open: gt, lt

  // Notes on the sheet:
  //   sub
  //   bne
  //   add
  //   and
  //   or
  //   lui
  //   ou seja, quando ALUOp = 0000
  //   So ocorre quando opCode = 000000
endmodule

module or32x1 (
  input  [31:0] in_32,
  output out_32
);

  or or_1 (out_32, in_32[0], in_32[1], in_32[2], in_32[3], in_32[4], in_32[5], in_32[6], in_32[7], in_32[8], in_32[9], in_32[10], in_32[11], in_32[12], in_32[13], in_32[14], in_32[15], in_32[17], in_32[18], in_32[19], in_32[20], in_32[21], in_32[22], in_32[23], in_32[24], in_32[25], in_32[26], in_32[27], in_32[28], in_32[29], in_32[30], in_32[31], in_32[16]);
endmodule

module address_spliter (
  input  [31:0] full_address,
  output a1,
  output [1:0] a1a0,
  output [23:0] address
);


  assign a1 = full_address[1];
  assign a1a0 = full_address[1:0];
  assign address = full_address[25:2];
endmodule

module ext_8_32 (
  input  [7:0] in_8,
  output [31:0] out_32
);


  assign out_32 = {{24{1'b0}}, in_8};
endmodule

module ext_16_32 (
  input  [15:0] in_16,
  output [31:0] out_32
);


  assign out_32 = {{16{1'b0}}, in_16};
endmodule

module sll_2 (
  input  [31:0] in_32,
  output [31:0] out_32
);


  assign out_32 = {in_32[29:0], 2'b00};
endmodule

module sll_16 (
  input  [31:0] in_32,
  output [31:0] out_32
);


  assign out_32 = {in_32[15:0], {16{1'b0}}};
endmodule

module bne_comparator (
  input  [31:0] in0_32,
  input  [31:0] in1_32,
  output [31:0] out_32
);

  Comparator #(.width(32)) comparator_1 (.a(in0_32), .b(in1_32), .eq(out_32[31]));  // open: gt, lt

  assign out_32[30:0] = {31{out_32[31]}};
endmodule

module target_calc (
  input  [25:0] jmp_target,
  input  [31:0] pc_plus_4,
  output [31:0] target_out
);

  wire [31:30] undriven;

  sll_2 sll_2_1 (.out_32(target_out), .in_32({undriven, pc_plus_4[31:28], jmp_target}));
endmodule
